# Fritzing sketch butterfingers (saved by Fritzing 0.9.3b)
circuit board: 7.75598cm x 8.21776cm
breadboards: 4

parts:
  Pololu_DRV1 = Pololu DRV8825 [package=SO16]
  Pololu_DRV2 = Pololu DRV8825 [package=SO16]
  Pololu_DRV3 = Pololu DRV8825 [package=SO16]
  Pololu_DRV4 = Pololu DRV8825 [package=SO16]
  Pololu_DRV5 = Pololu DRV8825 [package=SO16]
  LiPo+ = Pad [width=4 height=6 connect=center]
  GND = Pad [width=4 height=6 connect=center]
  24 = Pad [width=3 height=2 connect=center]
  25 = Pad [width=3 height=2 connect=center]
  26 = Pad [width=3 height=2 connect=center]
  Pad7 = Pad [width=3 height=2 connect=center]
  Pad8 = Pad [width=3 height=2 connect=center]
  Pad9 = Pad [width=3 height=2 connect=center]
  Pad10 = Pad [width=3 height=2 connect=center]
  Pad12 = Pad [width=3 height=2 connect=center]
  D1 = Pad [width=3 height=2 connect=center]
  D0 = Pad [width=3 height=2 connect=center]
  GND_2 = Pad [width=3 height=2 connect=center]
  Pad16 = Pad [width=3 height=2 connect=center]
  Pad17 = Pad [width=3 height=2 connect=center]
  Pad18 = Pad [width=3 height=2 connect=center]
  Pad19 = Pad [width=3 height=2 connect=center]
  Pad20 = Pad [width=3 height=2 connect=center]
  Pad21 = Pad [width=3 height=2 connect=center]
  M1-1 = Pad [width=3 height=4 connect=center]
  M1-2 = Pad [width=3 height=4 connect=center]
  M1-3 = Pad [width=3 height=4 connect=center]
  M1-4 = Pad [width=3 height=4 connect=center]
  M2-1 = Pad [width=3 height=4 connect=center]
  M2-2 = Pad [width=3 height=4 connect=center]
  M2-3 = Pad [width=3 height=4 connect=center]
  M2-4 = Pad [width=3 height=4 connect=center]
  M3-1 = Pad [width=3 height=4 connect=center]
  M3-2 = Pad [width=3 height=4 connect=center]
  M3-3 = Pad [width=3 height=4 connect=center]
  M3-4 = Pad [width=3 height=4 connect=center]
  M4-1 = Pad [width=3 height=4 connect=center]
  M4-2 = Pad [width=3 height=4 connect=center]
  M4-3 = Pad [width=3 height=4 connect=center]
  M4-4 = Pad [width=3 height=4 connect=center]
  M5-1 = Pad [width=3 height=4 connect=center]
  M5-2 = Pad [width=3 height=4 connect=center]
  M5-3 = Pad [width=3 height=4 connect=center]
  M5-4 = Pad [width=3 height=4 connect=center]
  Pad11 = Pad [width=3 height=2 connect=center]
  U1 = Voltage Regulator - 5V [package="TO220 [THT]"]
  Teensy1 = Teensy 3.6 (Basic)
  +5V = Pad [width=3 height=4 connect=center]
  GND_3 = Pad [width=3 height=4 connect=center]
  +5V_2 = Pad [width=3 height=4 connect=center]
  GND_4 = Pad [width=3 height=4 connect=center]
  LiPo+_2 = Pad [width=3 height=4 connect=center]
  3v3 = Pad [width=3 height=2 connect=center]

nets:
  GND: Pololu_DRV1.ENABLE, Pololu_DRV1.GND, Pololu_DRV2.ENABLE, Pololu_DRV2.GND, Pololu_DRV3.ENABLE, Pololu_DRV3.GND, Pololu_DRV4.ENABLE, Pololu_DRV4.GND, Pololu_DRV5.ENABLE, Pololu_DRV5.GND, GND.pad, GND_2.pad, U1.GND, Teensy1.GND, Teensy1.AGND, Teensy1.GND1, GND_3.pad, GND_4.pad
  N1: Pololu_DRV1.M0, Pololu_DRV2.M0, Pololu_DRV3.M0, Teensy1.A9/D23
  N2: Pololu_DRV1.M1, Pololu_DRV2.M1, Pololu_DRV3.M1, Teensy1.A8/D22
  N3: Pololu_DRV1.M2, Pololu_DRV2.M2, Pololu_DRV3.M2, Teensy1.A7/D21
  N4: Pololu_DRV1.RESET, Pololu_DRV2.RESET, Pololu_DRV3.RESET, Pololu_DRV4.RESET, Pololu_DRV5.RESET, U1.output_voltage, Teensy1.Vin, +5V.pad, +5V_2.pad
  N5: Pololu_DRV1.SLEEP, Teensy1.A6/D20
  N6: Pololu_DRV1.STEP, Teensy1.A5/D19
  N7: Pololu_DRV1.DIR, Teensy1.A4/D18
  N8: Pololu_DRV1.A2, M1-4.pad
  N9: Pololu_DRV1.A1, M1-3.pad
  N10: Pololu_DRV1.B1, M1-2.pad
  N11: Pololu_DRV1.B2, M1-1.pad
  N12: Pololu_DRV1.VMOT, Pololu_DRV2.VMOT, Pololu_DRV3.VMOT, Pololu_DRV4.VMOT, Pololu_DRV5.VMOT, LiPo+.pad, U1.input_voltage, LiPo+_2.pad
  N13: Pololu_DRV2.SLEEP, Teensy1.A3/D17
  N14: Pololu_DRV2.STEP, Teensy1.A2/D16
  N15: Pololu_DRV2.DIR, Teensy1.A1/D15
  N16: Pololu_DRV2.A2, M2-4.pad
  N17: Pololu_DRV2.A1, M2-3.pad
  N18: Pololu_DRV2.B1, M2-2.pad
  N19: Pololu_DRV2.B2, M2-1.pad
  N20: Pololu_DRV3.SLEEP, Teensy1.A22/DAC1
  N21: Pololu_DRV3.STEP, Teensy1.A21/DAC0
  N22: Pololu_DRV3.DIR, Teensy1.D39
  N23: Pololu_DRV3.A2, M3-4.pad
  N24: Pololu_DRV3.A1, M3-3.pad
  N25: Pololu_DRV3.B1, M3-2.pad
  N26: Pololu_DRV3.B2, M3-1.pad
  N27: Pololu_DRV4.M0, Pololu_DRV5.M0, Teensy1.D10
  N28: Pololu_DRV4.M1, Pololu_DRV5.M1, Teensy1.D9
  N29: Pololu_DRV4.M2, Pololu_DRV5.M2, Teensy1.D8
  N30: Pololu_DRV4.SLEEP, Teensy1.D4
  N31: Pololu_DRV4.STEP, Teensy1.D3
  N32: Pololu_DRV4.DIR, Teensy1.D2
  N33: Pololu_DRV4.A2, M4-4.pad
  N34: Pololu_DRV4.A1, M4-3.pad
  N35: Pololu_DRV4.B1, M4-2.pad
  N36: Pololu_DRV4.B2, M4-1.pad
  N37: Pololu_DRV5.SLEEP, Teensy1.D7
  N38: Pololu_DRV5.STEP, Teensy1.D6
  N39: Pololu_DRV5.DIR, Teensy1.D5
  N40: Pololu_DRV5.A2, M5-4.pad
  N41: Pololu_DRV5.A1, M5-3.pad
  N42: Pololu_DRV5.B1, M5-2.pad
  N43: Pololu_DRV5.B2, M5-1.pad
  N44: 24.pad, Teensy1.D24
  N45: 25.pad, Teensy1.D25
  N46: 26.pad, Teensy1.D26
  N47: Pad7.pad, Teensy1.D27
  N48: Pad8.pad, Teensy1.D28
  N49: Pad9.pad, Teensy1.D29
  N50: Pad10.pad, Teensy1.D30
  N51: Pad12.pad, Teensy1.D32
  N52: D1.pad, Teensy1.D1
  N53: D0.pad, Teensy1.D0
  N54: Pad16.pad, Teensy1.D38
  N55: Pad17.pad, Teensy1.D37
  N56: Pad18.pad, Teensy1.D36
  N57: Pad19.pad, Teensy1.D35
  N58: Pad20.pad, Teensy1.D34
  N59: Pad21.pad, Teensy1.D33
  N60: Pad11.pad, Teensy1.D31
  N61: Teensy1.3V3, Teensy1.3V3_1, 3v3.pad

notes:
  V1
  telpa

custom parts:
  Pololu DRV8825: The A4988 stepper motor driver carrier is a breakout board for Allegro’s A4988 microstepping bipolar stepper motor driver. The driver features adjustable current limiting, overcurrent and overtemperature protection, and five different microstep resolutions (down to 1/16-step). It operates from 8 – 35 V and can deliver up to approximately 1 A per phase without a heat sink or forced air flow (it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
  Teensy 3.6 (Basic): The Teensy is a complete USB-based microcontoller development system, in a very small footprint, capable of implementing many types of projects. All programming is done via the USB port. No special programmer is needed, only a standard micro-USB cable and a PC or Macintosh with a USB port.
